# Fritzing sketch HeliFlightControl (saved by Fritzing 0.9.3b)
breadboards: 1

parts:
  Receiver = IC, SIP package, 8 pins [chip_label=RX]
  Nano1 = Arduino Nano v2.3
  2S_Lipo = DC Power [voltage=8.4V]
  J1 = Basic Servo
  J2 = Basic Servo
  MPU6050_Gyro = IC, SIP package, 8 pins [chip_label=GY-521]
  Tail_motor = Vibration Motor- ROB-08449 [package=vibe-motor-10mm]
  Speed_Controller = IC, DIP package, 8 pins [chip_label=BL-ESC]

nets:
  N1: Receiver.pin1, Nano1.GND, MPU6050_Gyro.pin2
  VCC: Receiver.pin2, Nano1.+5V, J1.vcc, J2.vcc, MPU6050_Gyro.pin1, Speed_Controller.pin1
  N2: Receiver.pin3, Nano1.D8
  N3: Receiver.pin4, Nano1.D9
  N4: Receiver.pin5, Nano1.D10
  N5: Receiver.pin6, Nano1.D11
  N6: Nano1.D3, J2.pulse
  N7: Nano1.D4, J1.pulse
  N8: Nano1.D5, Speed_Controller.pin2
  N9: Nano1.A5, MPU6050_Gyro.pin3
  N10: Nano1.A4, MPU6050_Gyro.pin4
  N11: 2S_Lipo.V+, Speed_Controller.pin5
  GND: 2S_Lipo.V-, J1.gnd, J2.gnd, Speed_Controller.pin4
  N12: Tail_motor.+, Speed_Controller.pin8
  N13: Tail_motor.-, Speed_Controller.pin6
